# Fritzing sketch smartTFT (saved by Fritzing 0.9.3b)
stripboards: 1

parts:
  Bauteil1 = TXB0104 4-channel Bi-Directional Level Shifter
  JP3 = M16 [package=1x16_machine-pin-header_lock.004]
  Bauteil2 = TXB0104 4-channel Bi-Directional Level Shifter
  U2 = V_REG_LD1117VXX [package=78xxl]
  R1 = Photocell (LDR) [package=THT]
  R2 = Resistor [tolerance=±20% resistance=10k package=THT]
  Bauteil3 = Arduino Pro Mini v13  # not connected

nets:
  GND: Bauteil1.HV, Bauteil1.B1, Bauteil1.B2, Bauteil1.B3, Bauteil1.B4, Bauteil1.GND, Bauteil1.OE, Bauteil1.A4, Bauteil1.A3, Bauteil1.A2, Bauteil1.A1, Bauteil1.LV, JP3.1, JP3.2, JP3.3, JP3.4, JP3.5, JP3.6, JP3.7, JP3.8, JP3.9, JP3.10, JP3.11, JP3.12, JP3.13, JP3.14, JP3.15, JP3.16, Bauteil2.HV, Bauteil2.B1, Bauteil2.B2, Bauteil2.B3, Bauteil2.B4, Bauteil2.GND, Bauteil2.OE, Bauteil2.A4, Bauteil2.A3, Bauteil2.A2, Bauteil2.A1, Bauteil2.LV, U2.OUT, U2.GND, U2.IN, R1.pin_0, R1.pin_1, R2.Pin_0, R2.Pin_1

custom parts:
  TXB0104 4-channel Bi-Directional Level Shifter: Because the Arduino (and Basic Stamp) are 5V devices, and most modern sensors, displays, flash cards and modes are 3.3V-only, many makers find that they need to perform level shifting/conversion to protect the 3.3V device from 5V. Although one can use resistors to make a divider, for high speed transfers, the resistors can add a lot of slew and cause havoc that is tough to debug. For that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
